// Logisim project HW5_Q3.circ as structural Verilog: 1 circuit, main circuit main
module main (
  input  X,
  input  Y,
  output Z
);

  wire and_1_out, and_2_out, and_3_out, and_4_out, and_5_out, and_6_out, clock_1_out, d_ff_1_qn, j_k_ff_1_qn,
       not_1_out, not_2_out, or_2_out, or_3_out, or_4_out;

  not not_1 (not_1_out, X);
  not not_2 (not_2_out, Y);
  and and_1 (and_1_out, not_1_out, Y);
  and and_2 (and_2_out, X, j_k_ff_1_qn);
  and and_3 (and_3_out, not_2_out, d_ff_1_qn);
  buf and_4 (and_4_out, not_2_out);  // AND_Gate
  and and_5 (and_5_out, X, Y);
  and and_6 (and_6_out, Y, j_k_ff_1_qn);
  Clock clock_1 (.out(clock_1_out));
  or or_1 (Z, X, and_1_out);
  or or_2 (or_2_out, and_2_out, and_3_out);
  or or_3 (or_3_out, and_4_out, and_5_out);
  or or_4 (or_4_out, and_1_out, and_6_out);
  J_K_Flip_Flop j_k_ff_1 (
    .J(or_2_out), .clk(clock_1_out), .K(or_3_out), .Qn(j_k_ff_1_qn));  // open: Q, preset, en, reset
  D_Flip_Flop d_ff_1 (.clk(clock_1_out), .D(or_4_out), .Qn(d_ff_1_qn));  // open: Q, preset, en, reset

  // Notes on the sheet:
  //   ~xy
  //   xB
  //   ~yA
  //   ~yB
  //   xy
  //   yB
  //   Z
  //   Output, Z
  //   Kb
  //   Jb
  //   Da
  //   B
  //   A
endmodule
