// Logisim project HW5_Q4_Circut.circ as structural Verilog: 1 circuit, main circuit main
module main (
);

  wire A_q, B_q, C_q, clock_1_out, not_1_out, not_2_out, or_1_out, or_2_out, or_3_out, xnor_1_out;

  Clock clock_1 (.out(clock_1_out));
  or or_1 (or_1_out, not_2_out, B_q);
  or or_2 (or_2_out, B_q, C_q);
  or or_3 (or_3_out, not_1_out, not_2_out);
  xnor xnor_1 (xnor_1_out, B_q, A_q);
  not not_1 (not_1_out, A_q);
  J_K_Flip_Flop A (.J(or_1_out), .clk(clock_1_out), .K(or_2_out), .Q(A_q));  // open: Qn, preset, en, reset
  J_K_Flip_Flop B (.J(or_3_out), .clk(clock_1_out), .K(or_3_out), .Q(B_q));  // open: Qn, preset, en, reset
  not not_2 (not_2_out, C_q);
  J_K_Flip_Flop C (.J(xnor_1_out), .clk(clock_1_out), .K(A_q), .Q(C_q));  // open: Qn, preset, en, reset
endmodule
